// Logisim project ALU.circ as structural Verilog: 2 circuits, main circuit main
module main (
  input  [31:0] A,
  input  [4:0] in_2,
  input  [31:0] B,
  output [31:0] OUT,
  output [31:0] Hi,
  output [31:0] Lo
);

  wire BorrowRest, CoutAdd;
  wire [31:0] A0_Add, A1_Subs, A2_Mulu, A3_Mult, Add, B0_Add, B1_Subs, B2_Mulu, B3_Mult,
       demultiplexer_1_out4, demultiplexer_2_out4, Hi_Mulu, Lo_Mulu, Mult, Subs;

  // Probe on A
  // Probe on B
  Demultiplexer #(.select(5), .width(32), .enable("false")) demultiplexer_1 (
    .out0(A0_Add), .out1(A1_Subs), .out2(A2_Mulu), .out3(A3_Mult), .out4(demultiplexer_1_out4), .in(A),
    .sel(in_2));  // open: out5, out6, out7, out8, out9, out10, out11, out12, out13, out14, out15, out16, out17, out18, out19, out20, out21, out22, out23, out24, out25, out26, out27, out28, out29, out30, out31
  Demultiplexer #(.select(5), .width(32), .enable("false")) demultiplexer_2 (
    .out0(B0_Add), .out1(B1_Subs), .out2(B2_Mulu), .out3(B3_Mult), .out4(demultiplexer_2_out4), .in(B),
    .sel(in_2));  // open: out5, out6, out7, out8, out9, out10, out11, out12, out13, out14, out15, out16, out17, out18, out19, out20, out21, out22, out23, out24, out25, out26, out27, out28, out29, out30, out31
  Adder #(.width(32)) adder_1 (.a(A0_Add), .b(B0_Add), .out(Add), .cout(CoutAdd));  // open: cin
  Subtractor #(.width(32)) subtractor_1 (.a(A1_Subs), .b(B1_Subs), .out(Subs), .bout(BorrowRest));  // open: bin
  Multiplier #(.width(32)) multiplier_1 (.a(A2_Mulu), .b(B2_Mulu), .out(Hi_Mulu), .cout(Lo_Mulu));  // open: cin
  Multiplexer #(.select(5), .width(32), .enable("false")) multiplexer_1 (
    .in0(Add), .in1(Subs), .in2(Mult), .out(OUT), .sel(in_2));  // open: in3, in4, in5, in6, in7, in8, in9, in10, in11, in12, in13, in14, in15, in16, in17, in18, in19, in20, in21, in22, in23, in24, in25, in26, in27, in28, in29, in30, in31

  // Other names for the same wires on the sheet: Selector[4:0] = in_2
endmodule

module Mult_Signed (
  input  [31:0] A,
  input  [31:0] B,
  output [31:0] Hi,
  output [31:0] Lo
);

  wire [30:0] Carry, Carry_t, Carry_t_t, Carry_t_t_t, demultiplexer_1_out0, demultiplexer_1_out1,
       demultiplexer_1_out2, demultiplexer_1_out3, demultiplexer_2_out0, demultiplexer_2_out1,
       demultiplexer_2_out2, demultiplexer_2_out3, multiplier_1_out, multiplier_2_out, multiplier_3_out,
       multiplier_4_out, negator_2_out, negator_3_out, negator_4_out, negator_5_out;
  wire [31:0] negator_1_out, negator_6_out, negator_7_out, negator_8_out;

  // Probe on A
  // Probe on B
  Demultiplexer #(.select(2), .width(31), .enable("false")) demultiplexer_1 (
    .out0(demultiplexer_1_out0), .out1(demultiplexer_1_out1), .out2(demultiplexer_1_out2),
    .out3(demultiplexer_1_out3), .in(A[30:0]), .sel({B[31], A[31]}));
  Demultiplexer #(.select(2), .width(31), .enable("false")) demultiplexer_2 (
    .out0(demultiplexer_2_out0), .out1(demultiplexer_2_out1), .out2(demultiplexer_2_out2),
    .out3(demultiplexer_2_out3), .in(B[30:0]), .sel({B[31], A[31]}));
  Multiplier #(.width(31)) multiplier_1 (
    .a(demultiplexer_1_out0), .b(demultiplexer_2_out0), .out(multiplier_1_out), .cout(Carry));  // open: cin
  Negator #(.width(32)) negator_1 (.in({1'b0, Carry_t_t}), .out(negator_1_out));
  Negator #(.width(31)) negator_2 (.in(demultiplexer_1_out1), .out(negator_2_out));
  Multiplier #(.width(31)) multiplier_2 (
    .a(negator_2_out), .b(demultiplexer_2_out1), .out(multiplier_2_out), .cout(Carry_t_t));  // open: cin
  Negator #(.width(31)) negator_3 (.in(demultiplexer_2_out2), .out(negator_3_out));
  Negator #(.width(31)) negator_4 (.in(demultiplexer_1_out3), .out(negator_4_out));
  Negator #(.width(31)) negator_5 (.in(demultiplexer_2_out3), .out(negator_5_out));
  Negator #(.width(32)) negator_6 (.in({1'b0, Carry_t}), .out(negator_6_out));
  Multiplier #(.width(31)) multiplier_3 (
    .a(demultiplexer_1_out2), .b(negator_3_out), .out(multiplier_3_out), .cout(Carry_t));  // open: cin
  Multiplier #(.width(31)) multiplier_4 (
    .a(negator_4_out), .b(negator_5_out), .out(multiplier_4_out), .cout(Carry_t_t_t));  // open: cin
  Negator #(.width(32)) negator_7 (.in({1'b0, multiplier_2_out}), .out(negator_7_out));
  Negator #(.width(32)) negator_8 (.in({1'b0, multiplier_3_out}), .out(negator_8_out));
  Multiplexer #(.select(2), .width(32), .enable("false")) multiplexer_1 (
    .in0({1'b0, multiplier_1_out}), .in1(negator_7_out), .in2(negator_8_out), .in3({1'b0, multiplier_4_out}),
    .out(Hi), .sel({B[31], A[31]}));
  // Probe on Lo
  Multiplexer #(.select(2), .width(32), .enable("false")) multiplexer_2 (
    .in0({1'b0, Carry}), .in1(negator_1_out), .in2(negator_6_out), .in3({1'b0, Carry_t_t_t}), .out(Lo),
    .sel({B[31], A[31]}));
  // Probe on Hi

  // Other names for the same wires on the sheet: A_signed = A[31]; B_signed = B[31]

  // Notes on the sheet:
  //   ++
  //   -+
  //   +-
endmodule
