// Logisim project CACHE.circ as structural Verilog
module CACHE (
  input  [31:0] PC_Adr,
  input  CLK,
  input  [31:0] in_3,
  input  [31:0] in_4,
  input  [31:0] in_5,
  input  [31:0] in_6,
  input  Rst,
  input  Load,
  input  DesdeRAM,
  output [31:0] OUT,
  output [31:0] O1,
  output [31:0] O2,
  output Dirty,
  output [31:0] O2_2,
  output Valid,
  output [31:0] O4,
  output HINT
);

  wire C1, C2, C3, C4, Dirty1, Dirty2, Dirty3, Dirty4, Dirty_t, L1, L2, L3, L4, not_1_out, R1, R2, R3, R4,
       V1, V2, V3, V4;
  wire [11:0] multiplexer_1_out, T1, T2, T3, T4;
  wire [31:0] Out1, Out2, Out3, Out4, Out5, Out6, Out7, Out8, Out9, Out10, Out11, Out12, Out13, Out14, Out15,
       Out16;

  Demultiplexer #(.select(2), .enable("false")) demultiplexer_1 (
    .out0(C1), .out1(C2), .out2(C3), .out3(C4), .in(Load), .sel(PC_Adr[3:2]));
  not not_1 (not_1_out, DesdeRAM);
  Demultiplexer #(.select(2), .enable("false")) demultiplexer_2 (
    .out0(R1), .out1(R2), .out2(R3), .out3(R4), .in(DesdeRAM), .sel(PC_Adr[3:2]));
  and and_1 (Dirty_t, Load, not_1_out);
  Load_Guardar_RAM load_guardar_ram_1 ();
  Multiplexer #(.select(2), .width(12), .enable("false")) multiplexer_1 (
    .in0(T1), .in1(T2), .in2(T3), .in3(T4), .out(multiplexer_1_out), .sel(PC_Adr[3:2]));
  Comparator #(.width(12)) comparator_1 (.a(multiplexer_1_out), .b(PC_Adr[15:4]), .eq(HINT));  // open: gt, lt
  Register #(.width(12)) register_1 (.D(PC_Adr[15:4]), .en(L1), .Q(T1), .clk(CLK), .clr(Rst));
  Register #(.width(12)) register_2 (.D(PC_Adr[15:4]), .en(L2), .Q(T2), .clk(CLK), .clr(Rst));
  Register #(.width(12)) register_3 (.D(PC_Adr[15:4]), .en(L3), .Q(T3), .clk(CLK), .clr(Rst));
  Register #(.width(12)) register_4 (.D(PC_Adr[15:4]), .en(L4), .Q(T4), .clk(CLK), .clr(Rst));
  Register #(.width(32)) register_5 (.D(in_3), .en(L1), .Q(Out1), .clk(CLK), .clr(Rst));
  Register #(.width(32)) register_6 (.D(in_3), .en(L2), .Q(Out5), .clk(CLK), .clr(Rst));
  Register #(.width(32)) register_7 (.D(in_3), .en(L3), .Q(Out9), .clk(CLK), .clr(Rst));
  Register #(.width(32)) register_8 (.D(in_3), .en(L4), .Q(Out13), .clk(CLK), .clr(Rst));
  or or_1 (L1, C1, R1);
  or or_2 (L2, C2, R2);
  or or_3 (L3, C3, R3);
  or or_4 (L4, C4, R4);
  Multiplexer #(.select(2), .width(32), .enable("false")) multiplexer_2 (
    .in0(Out1), .in1(Out5), .in2(Out9), .in3(Out13), .out(O1), .sel(PC_Adr[3:2]));
  Multiplexer #(.select(2), .width(32), .enable("false")) multiplexer_3 (
    .in0(Out2), .in1(Out6), .in2(Out10), .in3(Out14), .out(O2), .sel(PC_Adr[3:2]));
  Multiplexer #(.select(2), .width(32), .enable("false")) multiplexer_4 (
    .in0(Out3), .in1(Out7), .in2(Out11), .in3(Out15), .out(O2_2), .sel(PC_Adr[3:2]));
  Multiplexer #(.select(2), .width(32), .enable("false")) multiplexer_5 (
    .in0(Out4), .in1(Out8), .in2(Out12), .in3(Out16), .out(O4), .sel(PC_Adr[3:2]));
  Register #(.width(32)) register_9 (.D(in_4), .en(L1), .Q(Out2), .clk(CLK), .clr(Rst));
  Register #(.width(32)) register_10 (.D(in_4), .en(L2), .Q(Out6), .clk(CLK), .clr(Rst));
  Register #(.width(32)) register_11 (.D(in_4), .en(L3), .Q(Out10), .clk(CLK), .clr(Rst));
  Register #(.width(32)) register_12 (.D(in_4), .en(L4), .Q(Out14), .clk(CLK), .clr(Rst));
  Multiplexer #(.select(2), .width(32), .enable("false")) multiplexer_6 (
    .in0(O1), .in1(O2), .in2(O2_2), .in3(O4), .out(OUT), .sel(PC_Adr[1:0]));
  Register #(.width(32)) register_13 (.D(in_5), .en(L1), .Q(Out3), .clk(CLK), .clr(Rst));
  Register #(.width(32)) register_14 (.D(in_5), .en(L2), .Q(Out7), .clk(CLK), .clr(Rst));
  Register #(.width(32)) register_15 (.D(in_5), .en(L3), .Q(Out11), .clk(CLK), .clr(Rst));
  Register #(.width(32)) register_16 (.D(in_5), .en(L4), .Q(Out15), .clk(CLK), .clr(Rst));
  Register #(.width(32)) register_17 (.D(in_6), .en(L1), .Q(Out4), .clk(CLK), .clr(Rst));
  Register #(.width(32)) register_18 (.D(in_6), .en(L2), .Q(Out8), .clk(CLK), .clr(Rst));
  Register #(.width(32)) register_19 (.D(in_6), .en(L3), .Q(Out12), .clk(CLK), .clr(Rst));
  Register #(.width(32)) register_20 (.D(in_6), .en(L4), .Q(Out16), .clk(CLK), .clr(Rst));
  Multiplexer #(.select(2), .enable("false")) multiplexer_7 (
    .in0(Dirty1), .in1(Dirty2), .in2(Dirty3), .in3(Dirty4), .out(Dirty), .sel(PC_Adr[3:2]));
  Multiplexer #(.select(2), .enable("false")) multiplexer_8 (
    .in0(V1), .in1(V2), .in2(V3), .in3(V4), .out(Valid), .sel(PC_Adr[3:2]));
  D_Flip_Flop u_VALID (.clk(CLK), .D(L1), .Q(V1), .en(L1), .reset(Rst));  // open: Qn, preset
  D_Flip_Flop VALID_2 (.clk(CLK), .D(L3), .Q(V2), .en(L3), .reset(Rst));  // open: Qn, preset
  D_Flip_Flop VALID_3 (.clk(CLK), .D(L3), .Q(V3), .en(L3), .reset(Rst));  // open: Qn, preset
  D_Flip_Flop VALID_4 (.clk(CLK), .D(L4), .Q(V4), .en(L4), .reset(Rst));  // open: Qn, preset
  D_Flip_Flop u_Dirty (.clk(CLK), .D(Dirty_t), .Q(Dirty1), .en(L1), .reset(Rst));  // open: Qn, preset
  D_Flip_Flop Dirty_2 (.clk(CLK), .D(Dirty_t), .Q(Dirty2), .en(L3), .reset(Rst));  // open: Qn, preset
  D_Flip_Flop Dirty_3 (.clk(CLK), .D(Dirty_t), .Q(Dirty3), .en(L3), .reset(Rst));  // open: Qn, preset
  D_Flip_Flop Dirty_4 (.clk(CLK), .D(Dirty_t), .Q(Dirty4), .en(L4), .reset(Rst));  // open: Qn, preset

  // Other names for the same wires on the sheet: D1[31:0] = in_3; D2[31:0] = in_4; D3[31:0] = in_5; D4[31:0] = in_6;
  //   O3[31:0] = O2_2; OFFSET[1:0] = PC_Adr[1:0]; INDEX[1:0] = PC_Adr[3:2]; TAG[11:0] = PC_Adr[15:4]
endmodule
