// Logisim project Control Unit.circ as structural Verilog: 4 circuits, main circuit main
module main (
);

  Control_Unit control_unit_1 ();  // open: Start, Reset, operacion, R_W, Read_Time, Write_Time, Wait, in_8, Load_Register_File, Escribir_RAM, RAM_Control, STOP, KBD_ENABLE, Load_Program_Counter, TTY_Enable, LoadMemory
endmodule

module Registro_de_Instrucciones (
  input  [31:0] Ram_Out_0,
  input  [31:0] Ram_Out_1,
  input  [31:0] Ram_Out_2,
  input  [31:0] Ram_Out_3,
  input  [1:0] Select_Instruction,
  input  Reloj,
  input  En,
  input  Reset,
  output [31:0] out_9
);

  wire [31:0] Instruction_0, Instruction_1, Instruction_2, Instruction_3;

  Register #(.width(32)) register_1 (.D(Ram_Out_0), .en(Reloj), .Q(Instruction_0), .clk(En), .clr(Reset));
  Register #(.width(32)) register_2 (.D(Ram_Out_1), .en(Reloj), .Q(Instruction_1), .clk(En), .clr(Reset));
  Register #(.width(32)) register_3 (.D(Ram_Out_2), .en(Reloj), .Q(Instruction_2), .clk(En), .clr(Reset));
  Register #(.width(32)) register_4 (.D(Ram_Out_3), .en(Reloj), .Q(Instruction_3), .clk(En), .clr(Reset));
  Multiplexer #(.select(2), .width(32), .enable("false")) multiplexer_1 (
    .in0(Instruction_0), .in1(Instruction_1), .in2(Instruction_2), .in3(Instruction_3), .out(out_9),
    .sel(Select_Instruction));

  // Other names for the same wires on the sheet: CLK = Reloj; Instruc[1:0] = Select_Instruction

  // Notes on the sheet:
  //   Data From Ram
  //   Selector de Instruccion
  //   Cosas de los Registro
  //   Out
endmodule

module Contador_de_Ciclos (
  input  [3:0] Read_Time,
  input  [3:0] Write_Time,
  input  Reloj,
  input  R_W,
  input  Reset,
  output Leido,
  output Escrito
);

  wire comparator_1_eq;
  wire [3:0] multiplexer_1_out, Registro_Contador_q, Time;

  Counter #(.width(4), .max('hf)) Registro_Contador (
    .Q(Registro_Contador_q), .clk(Reloj), .clr(Reset));  // open: load, D, count, carry
  Multiplexer #(.width(4), .enable("false")) multiplexer_1 (
    .in0(Read_Time), .in1(Write_Time), .out(multiplexer_1_out), .sel(R_W));
  Comparator #(.width(4), .mode("unsigned")) comparator_1 (
    .a(Registro_Contador_q), .b(Time), .eq(comparator_1_eq));  // open: gt, lt
  Demultiplexer #(.enable("false")) demultiplexer_1 (.out0(Leido), .out1(Escrito), .in(comparator_1_eq), .sel(R_W));
  Adder #(.width(4)) adder_1 (.a(multiplexer_1_out), .b(4'b0001), .out(Time));  // open: cin, cout

  // Other names for the same wires on the sheet: CLK = Reloj

  // Notes on the sheet:
  //   Entradas de Tiempo
  //   Contador de Ciclos del Reloj
endmodule

// esperar actualizacion PC
module Control_Unit (
  input  Start,
  input  Reset,
  input  [3:0] operacion,
  input  R_W,
  input  [3:0] Read_Time,
  input  [3:0] Write_Time,
  input  Wait,
  input  in_8,
  output Load_Register_File,
  output Escribir_RAM,
  output RAM_Control,
  output STOP,
  output KBD_ENABLE,
  output Load_Program_Counter,
  output TTY_Enable,
  output LoadMemory
);

  wire ALU_Tip_R_and_Tip_I, Camb_Instr, CLK, comparator_1_eq, d_ff_1_q, d_ff_2_q, d_ff_6_q, d_ff_9_q,
       demultiplexer_1_out0, demultiplexer_3_out0, demultiplexer_3_out1, demultiplexer_5_out0,
       demultiplexer_6_out0, demultiplexer_7_out0, demultiplexer_7_out1, demultiplexer_8_out0,
       demultiplexer_8_out1, EN_RND, END, Escribir, esperar_actualizacionPC_q, Jmp_nop_Jr, KBD, Leer,
       LeerNuevaLinea, Load, M1, M2, M3, M4, M5, Mov_Operation, not_1_out, or_1_out, or_2_out, or_3_out,
       or_4_out, or_9_out, or_10_out, or_11_out, or_12_out, Pop, Push, R_W_RF2, R_W_RF3, Rst, Rst_2;
  wire [3:0] adder_1_out, counter_1_q, multiplexer_1_out;

  Clock Reloj (.out(CLK));
  D_Flip_Flop d_ff_1 (.clk(CLK), .D(demultiplexer_1_out0), .Q(d_ff_1_q), .preset(or_1_out));  // open: Qn, en, reset
  or or_1 (or_1_out, Reset, not_1_out);
  not not_1 (not_1_out, Start);
  or or_2 (or_2_out, d_ff_1_q, END);
  or or_3 (or_3_out, Rst, Load);
  Demultiplexer #(.enable("false")) demultiplexer_1 (
    .out0(demultiplexer_1_out0), .out1(Rst), .in(or_2_out), .sel(Start));
  Counter #(.width(4), .max('hf)) counter_1 (
    .Q(counter_1_q), .clk(CLK), .clr(or_3_out));  // open: load, D, count, carry
  Multiplexer #(.width(4), .enable("false")) multiplexer_1 (
    .in0(Read_Time), .in1(Write_Time), .out(multiplexer_1_out), .sel(R_W));
  Adder #(.width(4)) adder_1 (.a(multiplexer_1_out), .b(4'b0001), .out(adder_1_out));  // open: cin, cout
  D_Flip_Flop Insruction_Read (.clk(CLK), .D(or_4_out), .Q(M5), .reset(Reset));  // open: Qn, preset, en
  or or_4 (or_4_out, Rst, LeerNuevaLinea, demultiplexer_3_out0);
  or or_5 (Escribir_RAM, M2, M4);
  Comparator #(.width(4)) comparator_1 (.a(counter_1_q), .b(adder_1_out), .eq(comparator_1_eq));  // open: gt, lt
  or or_6 (Load_Register_File, ALU_Tip_R_and_Tip_I, Mov_Operation, R_W_RF2, R_W_RF3, Push, EN_RND, KBD);
  Demultiplexer #(.enable("false")) demultiplexer_2 (.out0(Leer), .out1(Escribir), .in(comparator_1_eq), .sel(R_W));
  Demultiplexer #(.enable("false")) demultiplexer_3 (
    .out0(demultiplexer_3_out0), .out1(demultiplexer_3_out1), .in(M5), .sel(Leer));
  or or_7 (LoadMemory, demultiplexer_3_out1, Camb_Instr);
  D_Flip_Flop d_ff_2 (.clk(CLK), .D(LoadMemory), .Q(d_ff_2_q), .reset(Reset));  // open: Qn, preset, en
  Demultiplexer #(.select(4), .enable("false")) demultiplexer_4 (
    .out0(Jmp_nop_Jr), .out1(ALU_Tip_R_and_Tip_I), .out2(Mov_Operation), .out3(STOP), .out4(TTY_Enable),
    .out5(EN_RND), .out6(Pop), .out7(Push), .out8(Rst_2), .out9(Load), .out10(KBD), .in(d_ff_2_q),
    .sel(operacion));  // open: out11, out12, out13, out14, out15
  or or_8 (RAM_Control, M1, M2, M3, M4, M5);
  or or_9 (or_9_out, demultiplexer_5_out0, Pop);
  D_Flip_Flop d_ff_3 (.clk(CLK), .D(or_9_out), .Q(M3), .reset(Reset));  // open: Qn, preset, en
  or or_10 (or_10_out, demultiplexer_6_out0, Load);
  or or_11 (or_11_out, demultiplexer_7_out0, Rst_2);
  Demultiplexer #(.enable("false")) demultiplexer_5 (.out0(demultiplexer_5_out0), .out1(R_W_RF3), .in(M3), .sel(Leer));
  D_Flip_Flop d_ff_4 (.clk(CLK), .D(or_10_out), .Q(M1), .reset(Reset));  // open: Qn, preset, en
  D_Flip_Flop d_ff_5 (.clk(CLK), .D(or_11_out), .Q(M2), .reset(Reset));  // open: Qn, preset, en
  or or_12 (or_12_out, Push, demultiplexer_8_out0);
  D_Flip_Flop d_ff_6 (.clk(CLK), .D(TTY_Enable), .Q(d_ff_6_q), .reset(Reset));  // open: Qn, preset, en
  Demultiplexer #(.enable("false")) demultiplexer_6 (.out0(demultiplexer_6_out0), .out1(R_W_RF2), .in(M1), .sel(Leer));
  Demultiplexer #(.enable("false")) demultiplexer_7 (
    .out0(demultiplexer_7_out0), .out1(demultiplexer_7_out1), .in(M2), .sel(Escribir));
  D_Flip_Flop d_ff_7 (.clk(CLK), .D(or_12_out), .Q(M4), .reset(Reset));  // open: Qn, preset, en
  D_Flip_Flop d_ff_8 (.clk(CLK), .D(KBD), .Q(KBD_ENABLE), .reset(Reset));  // open: Qn, preset, en
  Demultiplexer #(.enable("false")) demultiplexer_8 (
    .out0(demultiplexer_8_out0), .out1(demultiplexer_8_out1), .in(M4), .sel(Escribir));
  D_Flip_Flop d_ff_9 (.clk(CLK), .D(demultiplexer_8_out1), .Q(d_ff_9_q), .reset(Reset));  // open: Qn, preset, en
  or or_13 (Load_Program_Counter, Jmp_nop_Jr, ALU_Tip_R_and_Tip_I, Mov_Operation, R_W_RF2, demultiplexer_7_out1, R_W_RF3, d_ff_9_q, EN_RND, KBD_ENABLE, d_ff_6_q);
  D_Flip_Flop esperar_actualizacionPC (
    .clk(CLK), .D(Load_Program_Counter), .Q(esperar_actualizacionPC_q));  // open: Qn, preset, en, reset
  Demultiplexer #(.enable("false")) demultiplexer_9 (
    .out0(Camb_Instr), .out1(LeerNuevaLinea), .in(esperar_actualizacionPC_q), .sel(in_8));
  D_Flip_Flop u_END (.clk(CLK), .D(STOP), .Q(END), .reset(Reset));  // open: Qn, preset, en

  // Other names for the same wires on the sheet: CargarNuevaLinea = in_8; CS = RAM_Control; E_KBD = KBD_ENABLE;
  //   Halt = STOP; Load_PC = Load_Program_Counter; LoadITMemory = LoadMemory; Op[3:0] = operacion;
  //   R_W_Cach = Escribir_RAM; R_W_Cach_0 = M2; R_W_Cach_1 = M4; R_W_RF = Load_Register_File;
  //   R_W_RF0 = ALU_Tip_R_and_Tip_I; R_W_RF1 = Mov_Operation; R_W_RF4 = Push; R_W_RF6 = KBD; R_W_RF5 = EN_RND;
  //   Random = EN_RND; Read_Tm[3:0] = Read_Time; Resert = Reset; Rst_1 = Load; Rst_3 = Pop; Store = Rst_2;
  //   TTY = TTY_Enable; TTY_EN = TTY_Enable; Write_Tm[3:0] = Write_Time

  // Notes on the sheet:
  //   cargar nueva linea
  //   Entradas
  //   Reloj
  //   Selector de Operacion
  //   Time
  //   Notas
  //   Esto es para leer y escribir
  //   Cargar nueva linea de instruccion 
  //   Esto me lo da la cache es wait no se dividenn casos
  //   INDLE
  //   No necesito los reset del contador ni el contador eso lo pasa la cache
  //   Control Unit
  //   Activa si se va a escribir en la RAM
  //   Activar el load de los registros
  //   Cargar info de la RAM
  //   Contador de ciclos
  //   Activa el Ram Control
  //   Jmp, nor, Jr
  //   Alu (Tipo R and Tipo I)
  //   Mover los registros
  //   Halt
  //   Operaciones
  //   Instrucciones de Memoria
  //   Cambio de instruccion
  //   OUTPUT DATA
endmodule
