// Logisim project InstructionDecoder.circ as structural Verilog
module InstructionDec (
  input  [31:0] Instruccion,
  input  LoadInstruction,
  input  Reset,
  input  Clock,
  output [5:0] Function,
  output [4:0] Shamt,
  output [4:0] Rd,
  output [4:0] Rt,
  output [4:0] Rs,
  output [15:0] Offset,
  output [25:0] Destino,
  output [5:0] OP_Code
);

  Register #(.width(32)) register_1 (
    .D(Instruccion), .en(LoadInstruction), .Q({OP_Code, Destino}), .clk(Clock), .clr(Reset));

  assign Function = Destino[5:0];
  assign Offset = Destino[15:0];
  assign Rd = Destino[15:11];
  assign Rs = Destino[25:21];
  assign Rt = Destino[20:16];
  assign Shamt = Destino[10:6];

  // Other names for the same wires on the sheet: Instruction[31:0] = Instruccion; Load = LoadInstruction

  // Notes on the sheet:
  //   INPUTS
  //   Instrucciones de Tipo R:
  //   OP-Code: (6-bits) , Rs (5-bits)  , Rt (5-bits) , Rd(5-bits)  , Shamt(5-bits) , Function(6-bits)  
  //   Instrucciones de Tipo I
  //   OP-Code: (6-bits) , Rs (5-bits)  , Rt (5-bits) , Imm-Constante-Offset 16-bits
  //   Instrucciones de Tipo J
  //   OP-Code: (6-bits) , addr(destino) 26-bits
  //   Divide la  Instruccion
  //   OUTPUTS
endmodule

module DivideOpCode (
  input  [5:0] OP_Code,
  output Op_00_0000,
  output Op_11_1000,
  output Op_11_1111,
  output I,
  output J,
  output R
);

  wire and_1_out, and_2_out, and_4_out, and_5_out, and_6_out, and_7_out, and_8_out, and_9_out, and_10_out,
       and_11_out, and_12_out, and_13_out, and_14_out, and_15_out, and_17_out, and_18_out, and_19_out,
       and_20_out;

  and and_1 (and_1_out, ~OP_Code[0], OP_Code[1], ~OP_Code[2]);  // AND_Gate
  and and_2 (and_2_out, ~OP_Code[3], ~OP_Code[4], ~OP_Code[5]);  // AND_Gate
  and and_3 (J, and_1_out, and_2_out);
  and and_4 (and_4_out, ~OP_Code[4], ~OP_Code[5]);  // AND_Gate
  and and_5 (and_5_out, ~OP_Code[4], OP_Code[5]);  // AND_Gate
  and and_6 (and_6_out, ~OP_Code[0], ~OP_Code[2], OP_Code[3]);  // AND_Gate
  and and_7 (and_7_out, ~OP_Code[0], ~OP_Code[1], OP_Code[2]);  // AND_Gate
  and and_8 (and_8_out, OP_Code[1], OP_Code[2], ~OP_Code[3]);  // AND_Gate
  and and_9 (and_9_out, OP_Code[0], ~OP_Code[1], ~OP_Code[3]);  // AND_Gate
  and and_10 (and_10_out, OP_Code[0], OP_Code[1], ~OP_Code[2]);  // AND_Gate
  and and_11 (and_11_out, and_6_out, and_4_out);
  and and_12 (and_12_out, and_7_out, and_4_out);
  and and_13 (and_13_out, and_8_out, and_4_out);
  and and_14 (and_14_out, and_9_out, and_4_out);
  and and_15 (and_15_out, and_10_out, and_5_out);
  and and_16 (Op_11_1111, OP_Code[0], OP_Code[1], OP_Code[2], OP_Code[3], OP_Code[4], OP_Code[5]);
  and and_17 (and_17_out, ~OP_Code[0], ~OP_Code[1], ~OP_Code[2]);  // AND_Gate
  and and_18 (and_18_out, OP_Code[3], OP_Code[4], OP_Code[5]);
  and and_19 (and_19_out, ~OP_Code[0], ~OP_Code[1], ~OP_Code[2]);  // AND_Gate
  and and_20 (and_20_out, ~OP_Code[3], ~OP_Code[4], ~OP_Code[5]);  // AND_Gate
  and and_21 (Op_11_1000, and_17_out, and_18_out);
  and and_22 (Op_00_0000, and_19_out, and_20_out);
  or or_1 (I, and_11_out, and_12_out, and_13_out, and_14_out, and_15_out);
  or or_2 (R, Op_11_1111, Op_11_1000, Op_00_0000);

  // Other names for the same wires on the sheet: _00_0000 = Op_00_0000; _11_1000 = Op_11_1000; _11_1111 = Op_11_1111;
  //   B0 = OP_Code[0]; B1 = OP_Code[1]; B2 = OP_Code[2]; B3 = OP_Code[3]; B4 = OP_Code[4]; B5 = OP_Code[5]

  // Notes on the sheet:
  //   OP-Code TIPO J
  //   OP-Code TIPO I
  //   OP-Code TIPO R
endmodule

module Procesar (
  input  [31:0] INSTRUCTION,
  input  LOAD,
  input  CLK,
  input  RESET
);

  wire Rw_HI_LO;
  wire [1:0] InputRF_Selector;
  wire [3:0] ALU_OP;
  wire [5:0] Function, OPCOde;

  InstructionDec instructiondec_1 (
    .Instruccion(INSTRUCTION), .LoadInstruction(LOAD), .Reset(RESET), .Clock(CLK), .Function(Function),
    .OP_Code(OPCOde));  // open: Shamt, Rd, Rt, Rs, Offset, Destino
  MOV_Op mov_op_1 (.OP_Code(OPCOde), .Function(Function), .RW(Rw_HI_LO), .Selector_Input_RF(InputRF_Selector));
  ALUOP_DECODER aluop_decoder_1 (.OP_Code(OPCOde), .Function(Function), .ALUOP(ALU_OP));
endmodule

module ALUOP_DECODER (
  input  [5:0] OP_Code,
  input  [5:0] Function,
  output [3:0] ALUOP
);

  wire _00_0000, _01_1000, _01_1001, _01_1010, _01_1011, _10_0000, _10_0010, _10_0100, _10_0101, _10_0111,
       _10_1000, _10_1010, _10_1011, ADD, ADDI, AND, and_1_out, and_2_out, and_3_out, and_4_out, and_5_out,
       and_7_out, and_8_out, and_10_out, and_11_out, and_13_out, and_16_out, and_17_out, and_18_out,
       and_19_out, and_20_out, and_21_out, and_22_out, and_23_out, and_24_out, and_26_out, and_31_out,
       and_32_out, and_33_out, and_34_out, and_35_out, and_36_out, and_37_out, and_38_out, and_39_out,
       and_40_out, and_46_out, and_47_out, and_48_out, and_49_out, and_50_out, and_51_out, and_52_out,
       and_53_out, ANDI, DIV, DIVU, MULT, MULU, NADA, NOR, OR, or_1_out, or_2_out, or_3_out, or_4_out,
       or_5_out, or_6_out, or_7_out, or_8_out, or_9_out, or_10_out, or_11_out, or_12_out, ORI, SLT, SLTI,
       SLTIU, SLTU, SUBS, XOR, XORI;

  and and_1 (and_1_out, ~OP_Code[0], ~OP_Code[1], ~OP_Code[2]);  // AND_Gate
  and and_2 (and_2_out, ~OP_Code[3], ~OP_Code[4], ~OP_Code[5]);  // AND_Gate
  and and_3 (and_3_out, ~OP_Code[0], ~OP_Code[1], ~OP_Code[2]);  // AND_Gate
  and and_4 (and_4_out, OP_Code[3], ~OP_Code[4], ~OP_Code[5]);  // AND_Gate
  and and_5 (and_5_out, ~Function[0], ~Function[1], ~Function[2]);  // AND_Gate
  and and_6 (_10_0000, and_5_out, and_7_out);
  and and_7 (and_7_out, ~Function[3], ~Function[4], Function[5]);  // AND_Gate
  and and_8 (and_8_out, ~Function[0], Function[1], ~Function[2]);  // AND_Gate
  and and_9 (_10_0010, and_8_out, and_10_out);
  and and_10 (and_10_out, ~Function[3], ~Function[4], Function[5]);  // AND_Gate
  and and_11 (and_11_out, Function[0], Function[1], Function[2]);
  and and_12 (_10_0111, and_11_out, and_13_out);
  and and_13 (and_13_out, ~Function[3], ~Function[4], Function[5]);  // AND_Gate
  and and_14 (_00_0000, and_1_out, and_2_out);
  and and_15 (ADDI, and_3_out, and_4_out);
  and and_16 (and_16_out, OP_Code[3], ~OP_Code[4], ~OP_Code[5]);  // AND_Gate
  and and_17 (and_17_out, OP_Code[3], ~OP_Code[4], ~OP_Code[5]);  // AND_Gate
  and and_18 (and_18_out, ~Function[0], ~Function[1], ~Function[2]);  // AND_Gate
  and and_19 (and_19_out, Function[3], Function[4], ~Function[5]);  // AND_Gate
  and and_20 (and_20_out, Function[0], ~Function[1], ~Function[2]);  // AND_Gate
  and and_21 (and_21_out, Function[3], Function[4], ~Function[5]);  // AND_Gate
  and and_22 (and_22_out, ~Function[0], ~Function[1], ~Function[2]);  // AND_Gate
  and and_23 (and_23_out, Function[3], ~Function[4], Function[5]);  // AND_Gate
  and and_24 (and_24_out, ~OP_Code[0], ~OP_Code[1], OP_Code[2]);  // AND_Gate
  and and_25 (ANDI, and_24_out, and_16_out);
  and and_26 (and_26_out, OP_Code[0], ~OP_Code[1], OP_Code[2]);  // AND_Gate
  and and_27 (ORI, and_26_out, and_17_out);
  and and_28 (_01_1000, and_18_out, and_19_out);
  and and_29 (_01_1001, and_20_out, and_21_out);
  and and_30 (_10_1000, and_22_out, and_23_out);
  or or_1 (or_1_out, ADD, ADDI);
  or or_2 (or_2_out, AND, ANDI);
  or or_3 (or_3_out, OR, ORI);
  or or_4 (or_4_out, XOR, XORI);
  or or_5 (or_5_out, SLTU, SLTIU);
  or or_6 (or_6_out, SLT, SLTI);
  and and_31 (and_31_out, ~OP_Code[0], OP_Code[1], OP_Code[2]);  // AND_Gate
  and and_32 (and_32_out, OP_Code[3], ~OP_Code[4], ~OP_Code[5]);  // AND_Gate
  and and_33 (and_33_out, ~OP_Code[0], OP_Code[1], ~OP_Code[2]);  // AND_Gate
  and and_34 (and_34_out, OP_Code[3], ~OP_Code[4], ~OP_Code[5]);  // AND_Gate
  and and_35 (and_35_out, ~Function[0], Function[1], ~Function[2]);  // AND_Gate
  and and_36 (and_36_out, Function[3], Function[4], ~Function[5]);  // AND_Gate
  and and_37 (and_37_out, Function[0], Function[1], ~Function[2]);  // AND_Gate
  and and_38 (and_38_out, Function[3], Function[4], ~Function[5]);  // AND_Gate
  and and_39 (and_39_out, ~Function[0], Function[1], ~Function[2]);  // AND_Gate
  and and_40 (and_40_out, Function[3], ~Function[4], Function[5]);  // AND_Gate
  and and_41 (XORI, and_31_out, and_32_out);
  and and_42 (SLTI, and_33_out, and_34_out);
  and and_43 (_01_1010, and_35_out, and_36_out);
  and and_44 (_01_1011, and_37_out, and_38_out);
  and and_45 (_10_1010, and_39_out, and_40_out);
  Priority_Encoder #(.select(4)) priority_encoder_1 (
    .in0(or_1_out), .in1(SUBS), .in2(or_2_out), .in3(or_3_out), .in4(NOR), .in5(or_4_out), .in6(or_5_out),
    .in7(or_6_out), .in8(MULU), .in9(MULT), .in10(DIVU), .in11(DIV), .in15(NADA), .out(ALUOP));  // open: in12, in13, in14, gs, en_out, en_in
  and and_46 (and_46_out, ~Function[0], ~Function[1], Function[2]);  // AND_Gate
  and and_47 (and_47_out, ~Function[3], ~Function[4], Function[5]);  // AND_Gate
  and and_48 (and_48_out, Function[0], ~Function[1], Function[2]);  // AND_Gate
  and and_49 (and_49_out, ~Function[3], ~Function[4], Function[5]);  // AND_Gate
  and and_50 (and_50_out, Function[0], Function[1], ~Function[2]);  // AND_Gate
  and and_51 (and_51_out, Function[3], ~Function[4], Function[5]);  // AND_Gate
  and and_52 (and_52_out, OP_Code[0], OP_Code[1], ~OP_Code[2]);  // AND_Gate
  and and_53 (and_53_out, OP_Code[3], ~OP_Code[4], ~OP_Code[5]);  // AND_Gate
  and and_54 (_10_0100, and_46_out, and_47_out);
  and and_55 (_10_0101, and_48_out, and_49_out);
  and and_56 (_10_1011, and_50_out, and_51_out);
  and and_57 (SLTIU, and_52_out, and_53_out);
  or or_7 (or_7_out, ADD, ADDI);
  or or_8 (or_8_out, AND, ANDI);
  or or_9 (or_9_out, OR, ORI);
  or or_10 (or_10_out, XOR, XORI);
  or or_11 (or_11_out, SLTU, SLTIU);
  or or_12 (or_12_out, SLT, SLTI);
  and and_58 (ADD, _00_0000, _10_0000);
  and and_59 (SUBS, _00_0000, _10_0010);
  and and_60 (MULT, _00_0000, _01_1000);
  and and_61 (MULU, _00_0000, _01_1001);
  and and_62 (DIV, _00_0000, _01_1010);
  and and_63 (DIVU, _00_0000, _01_1011);
  and and_64 (AND, _00_0000, _10_0100);
  and and_65 (OR, _00_0000, _10_0101);
  and and_66 (NOR, _00_0000, _10_0111);
  and and_67 (XOR, _00_0000, _10_1000);
  and and_68 (SLT, _00_0000, _10_1010);
  and and_69 (SLTU, _00_0000, _10_1011);
  and and_70 (NADA, ~or_7_out, ~SUBS, ~or_8_out, ~or_9_out, ~NOR, ~or_10_out, ~or_11_out, ~or_12_out, ~MULU, ~MULT, ~DIVU, ~DIV);  // AND_Gate

  // Other names for the same wires on the sheet: F0 = Function[0]; F1 = Function[1]; F2 = Function[2];
  //   F3 = Function[3]; F4 = Function[4]; F5 = Function[5]; B0 = OP_Code[0]; B1 = OP_Code[1]; B2 = OP_Code[2];
  //   B3 = OP_Code[3]; B4 = OP_Code[4]; B5 = OP_Code[5]

  // Notes on the sheet:
  //   INPUTS
  //   OPCODE R
  //   DECODIFICA LA OPERACION LOGICA - ARITEMTICA PARA QUE SEA ENTENDIDA POR EL ALU
  //   FUNCTION 
  //   OUTPUT
  //   OPCODE I
  //   OPCODE R + FUNCTION
endmodule

module MOV_Op (
  input  [5:0] OP_Code,
  input  [5:0] Function,
  output RW,
  output [1:0] Selector_Input_RF
);

  wire _00_0000, _01_0000, _01_0010, and_1_out, and_2_out, and_6_out, and_7_out, and_9_out, and_10_out,
       and_11_out, Rd____Hi, Rd____Lo;

  and and_1 (and_1_out, ~OP_Code[0], ~OP_Code[1], ~OP_Code[2]);  // AND_Gate
  and and_2 (and_2_out, ~OP_Code[3], ~OP_Code[4], ~OP_Code[5]);  // AND_Gate
  and and_3 (_00_0000, and_1_out, and_2_out);
  and and_4 (Rd____Hi, _00_0000, _01_0000);
  and and_5 (Rd____Lo, _00_0000, _01_0010);
  and and_6 (and_6_out, ~Function[0], ~Function[1], ~Function[2]);  // AND_Gate
  and and_7 (and_7_out, ~Function[3], Function[4], ~Function[5]);  // AND_Gate
  and and_8 (_01_0000, and_6_out, and_7_out);
  and and_9 (and_9_out, ~Rd____Hi, ~Rd____Lo);  // AND_Gate
  Priority_Encoder #(.select(2)) priority_encoder_1 (
    .in0(and_9_out), .in1(Rd____Hi), .in2(Rd____Lo), .out(Selector_Input_RF));  // open: in3, gs, en_out, en_in
  and and_10 (and_10_out, ~Function[0], Function[1], ~Function[2]);  // AND_Gate
  and and_11 (and_11_out, ~Function[3], Function[4], ~Function[5]);  // AND_Gate
  or or_1 (RW, Rd____Hi, Rd____Lo);
  and and_12 (_01_0010, and_10_out, and_11_out);

  // Other names for the same wires on the sheet: F0 = Function[0]; F1 = Function[1]; F2 = Function[2];
  //   F3 = Function[3]; F4 = Function[4]; F5 = Function[5]; B0 = OP_Code[0]; B1 = OP_Code[1]; B2 = OP_Code[2];
  //   B3 = OP_Code[3]; B4 = OP_Code[4]; B5 = OP_Code[5]

  // Notes on the sheet:
  //   INPUTS
endmodule

module BranchDecoder (
  input  [5:0] OP_Code,
  input  [5:0] Function,
  input  Rs__Rt
);


  // Other names for the same wires on the sheet: F0 = Function[0]; F1 = Function[1]; F2 = Function[2];
  //   F3 = Function[3]; F4 = Function[4]; F5 = Function[5]; B0 = OP_Code[0]; B1 = OP_Code[1]; B2 = OP_Code[2];
  //   B3 = OP_Code[3]; B4 = OP_Code[4]; B5 = OP_Code[5]

  // Notes on the sheet:
  //   INPUTS
endmodule
